# Fritzing sketch BraillePrinterScheme (saved by Fritzing 0.9.9b)
breadboards: 1

parts:
  Raspberry_Pi_1 = Raspberry Pi 3 [part_number=RPI-3-V1.2]
  U1 = BATTERY-2 [package=battery-aaa]
  Mod1 = KY-019 5V Relay Module [package="Breakout board"]
  M2 = Stepper Motor - Bipolar
  M3 = Stepper Motor - Bipolar
  L298N1 = L298N DC motor driver
  L298N2 = L298N DC motor driver
  L1 = Solenoid

nets:
  N1: Raspberry_Pi_1.GPIO2, Raspberry_Pi_1.5V, Mod1.+, L298N1.5V#7, L298N2.5V#7
  N2: Raspberry_Pi_1.GPIO6, L298N2.IN4
  N3: Raspberry_Pi_1.GPIO13, L298N2.IN3
  N4: Raspberry_Pi_1.GPIO19, L298N2.IN2
  N5: Raspberry_Pi_1.GPIO26, L298N2.IN1
  N6: Raspberry_Pi_1.GPIO21, L298N1.IN4
  N7: Raspberry_Pi_1.GPIO20, L298N1.IN3
  N8: Raspberry_Pi_1.GPIO16, L298N1.IN2
  N9: Raspberry_Pi_1.GPIO12, L298N1.IN1
  N10: Raspberry_Pi_1.GPIO18, Mod1.S
  GND: Raspberry_Pi_1.GND, U1.-1, Mod1.-, L298N1.GND, L298N2.GND, L1.pin1
  12V: U1.+1, Mod1.NO, L298N1.12V, L298N2.12V
  N11: Mod1.Common, L1.pin2
  N12: M2.A, L298N2.OUT2
  N13: M2.C, L298N2.OUT1
  N14: M2.B, L298N2.OUT4
  N15: M2.D, L298N2.OUT3
  N16: M3.A, L298N1.OUT2
  N17: M3.C, L298N1.OUT1
  N18: M3.B, L298N1.OUT4
  N19: M3.D, L298N1.OUT3
  N20: L298N1.5V#9, L298N1.ENA
  N21: L298N1.5V#10, L298N1.ENB
  N22: L298N2.5V#9, L298N2.ENA
  N23: L298N2.5V#10, L298N2.ENB

notes:
  12 V supply with minimum of 1.8 A

custom parts:
  KY-019 5V Relay Module: KY-019 5V Relay module, used to control AC circuits. (Special thanks to vanepp for fixing the PCB holes and other errors)
  L298N DC motor driver: 2x DC motor driver with 78M05 positive voltage regulator (7..35 V) L298N: max 46 V, 2 A Set 5 V Enable jumper to enable 5 V regultor (needed for the L298N) and +5 V output at screw terminal or supply external +5 V at screw terminal Set ENA and/or ENB to +5 V to enable motor permanently or supply ENA and/or ENB with PWM signal IN1 and IN2 set rotation directory for motor A (OUT1/OUT2) IN2 and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
